// Logisim project TIA.circ as structural Verilog: 18 circuits, main circuit main
module main (
  input  in_1,
  input  RSYNC,
  input  LRHB,
  input  HMOVE,
  input  RHB,
  output H2,
  output H1,
  output SHB,
  output SEC,
  output MOTCK
);

  wire and_1_out, and_2_out, and_3_out, and_4_out, and_5_out, buffer_1_out, d1r_1_out_5, d1r_2_out_5,
       d1r_3_out_5, d1r_4_out_5, d1r_5_out_5, d1r_6_out_5, dl_1_out, f1_1_nq, f1_1_q, f1_2_nq, f1_2_q,
       nfet_1_out_3, nfet_2_out_3, nfet_3_out_3, nfet_4_out_3, nfet_5_out_3, nor_1_out, nor_2_out, nor_3_out,
       nor_4_out, nor_5_out, nor_6_out, nor_7_out, nor_8_out, nor_9_out, nor_10_out, nor_11_out, nor_12_out,
       nor_13_out, not_1_out, not_2_out, not_3_out, not_4_out, not_5_out, not_6_out, not_7_out, not_8_out,
       not_9_out, not_10_out, not_11_out, not_12_out, not_13_out, not_14_out, not_c_1_out_3;

  NOR_c nor_c_1 (.B(not_1_out), .A(not_c_1_out_3), .out_4(MOTCK), .C(nor_1_out));
  not not_1 (not_1_out, dl_1_out);
  nor nor_1 (nor_1_out, not_c_1_out_3, not_1_out);
  nFet nfet_1 (.in_2(nor_2_out), .out_3(nfet_1_out_3), .in_1(H2));
  buf buffer_1 (buffer_1_out, nfet_1_out_3);
  buf buffer_2 (SEC, nfet_2_out_3);
  nFet nfet_2 (.in_2(buffer_1_out), .out_3(nfet_2_out_3), .in_1(H1));
  nor nor_2 (nor_2_out, nfet_3_out_3, nor_3_out);
  nor nor_3 (nor_3_out, nor_2_out, HMOVE);
  nFet nfet_3 (.in_2(SEC), .out_3(nfet_3_out_3), .in_1(H2));
  nor nor_4 (nor_4_out, SEC, nor_5_out);
  nor nor_5 (nor_5_out, nor_4_out, SHB);
  and and_1 (and_1_out, nor_4_out, RHB);
  nor nor_6 (nor_6_out, and_1_out, and_2_out);
  and and_2 (and_2_out, LRHB, nor_5_out);
  not not_2 (not_2_out, nor_6_out);
  DL dl_1 (.out(dl_1_out), .in(not_2_out), .H1(H1), .H2(H2), .R(SHB));
  Button OSC ();  // open: out
  not not_3 (not_3_out, in_1);
  NOT_c not_c_1 (.B(not_3_out), .A(not_4_out), .out_3(not_c_1_out_3));
  not not_4 (not_4_out, not_3_out);
  not not_5 (not_5_out, not_6_out);
  NOT_c not_c_2 (.B(not_6_out), .A(not_5_out), .out_3(SHB));
  F1 f1_1 (.nS(f1_2_q), .nR(f1_2_nq), .Q(f1_1_q), .nQ(f1_1_nq), .CK(not_c_1_out_3), .R(RSYNC));
  nFet nfet_4 (.in_2(not_7_out), .out_3(nfet_4_out_3), .in_1(H2));
  not not_6 (not_6_out, nfet_4_out_3);
  F1 f1_2 (.nS(f1_1_nq), .nR(f1_1_q), .Q(f1_2_q), .nQ(f1_2_nq), .CK(not_c_1_out_3), .R(RSYNC));
  nFet nfet_5 (.in_2(nor_7_out), .out_3(nfet_5_out_3), .in_1(H1));
  not not_7 (not_7_out, nfet_5_out_3);
  not not_8 (not_8_out, f1_2_nq);
  nor nor_7 (nor_7_out, and_3_out, nor_10_out, and_4_out);
  nor nor_8 (nor_8_out, f1_1_nq, f1_2_nq);
  NOR_c nor_c_2 (.B(f1_1_nq), .A(f1_2_nq), .out_4(H2), .C(nor_8_out));
  nor nor_9 (nor_9_out, f1_1_q, f1_2_q);
  NOR_c nor_c_3 (.B(f1_1_q), .A(f1_2_q), .out_4(H1), .C(nor_9_out));
  nor nor_10 (nor_10_out, not_8_out, nor_11_out);
  nor nor_11 (nor_11_out, nor_10_out, RSYNC);
  and and_3 (and_3_out, ~not_9_out, ~not_10_out, ~not_11_out, ~not_12_out, ~not_13_out, ~not_14_out);  // AND_Gate
  and and_4 (and_4_out, ~d1r_1_out_5, ~not_10_out, ~d1r_3_out_5, ~not_12_out, ~d1r_5_out_5, ~d1r_6_out_5);  // AND_Gate
  D1R d1r_1 (.in_3(nor_12_out), .out_5(d1r_1_out_5), .in_1(H1), .in_2(H2), .in_4(SHB));
  D1R d1r_2 (.in_3(d1r_1_out_5), .out_5(d1r_2_out_5), .in_1(H1), .in_2(H2), .in_4(SHB));
  not not_9 (not_9_out, d1r_1_out_5);
  not not_10 (not_10_out, d1r_2_out_5);
  nor nor_12 (nor_12_out, nor_13_out, and_5_out);
  D1R d1r_3 (.in_3(d1r_2_out_5), .out_5(d1r_3_out_5), .in_1(H1), .in_2(H2), .in_4(SHB));
  not not_11 (not_11_out, d1r_3_out_5);
  nor nor_13 (nor_13_out, not_14_out, d1r_5_out_5);
  and and_5 (and_5_out, not_14_out, d1r_5_out_5);
  D1R d1r_4 (.in_3(d1r_3_out_5), .out_5(d1r_4_out_5), .in_1(H1), .in_2(H2), .in_4(SHB));
  not not_12 (not_12_out, d1r_4_out_5);
  D1R d1r_5 (.in_3(d1r_4_out_5), .out_5(d1r_5_out_5), .in_1(H1), .in_2(H2), .in_4(SHB));
  not not_13 (not_13_out, d1r_5_out_5);
  D1R d1r_6 (.in_3(d1r_5_out_5), .out_5(d1r_6_out_5), .in_1(H1), .in_2(H2), .in_4(SHB));
  not not_14 (not_14_out, d1r_6_out_5);
endmodule

module NOT_c (
  input  B,
  input  A,
  output out_3
);

  wire and_1_out, pull_resistor_1_node, pull_resistor_2_node;

  and and_1 (and_1_out, ~B, A);  // AND_Gate
  Pull_Resistor pull_resistor_1 (.node(pull_resistor_1_node));
  assign out_3 = B ? pull_resistor_1_node : 1'bz;  // Controlled_Buffer controlled_buffer_1
  Pull_Resistor #(.pull(1)) pull_resistor_2 (.node(pull_resistor_2_node));
  assign out_3 = and_1_out ? pull_resistor_2_node : 1'bz;  // Controlled_Buffer controlled_buffer_2
endmodule

module NOR_c (
  input  C,
  input  B,
  input  A,
  output out_4
);

  wire and_1_out, nand_1_out, pull_resistor_1_node, pull_resistor_2_node;

  nand nand_1 (nand_1_out, ~B, ~A);  // NAND_Gate
  Pull_Resistor pull_resistor_1 (.node(pull_resistor_1_node));
  assign out_4 = nand_1_out ? pull_resistor_1_node : 1'bz;  // Controlled_Buffer controlled_buffer_1
  and and_1 (and_1_out, C, ~B, ~A);  // AND_Gate
  Pull_Resistor #(.pull(1)) pull_resistor_2 (.node(pull_resistor_2_node));
  assign out_4 = and_1_out ? pull_resistor_2_node : 1'bz;  // Controlled_Buffer controlled_buffer_2
endmodule

module F1 (
  input  CK,
  input  nS,
  input  nR,
  input  R,
  output Q,
  output nQ
);

  wire and_1_out, and_2_out, nor_1_out, nor_2_out, nor_3_out, nor_4_out;

  nor nor_1 (nor_1_out, nS, CK);
  nor nor_2 (nor_2_out, CK, nR);
  nor nor_3 (nor_3_out, nor_1_out, nor_4_out);
  nor nor_4 (nor_4_out, nor_3_out, R, nor_2_out);
  and and_1 (and_1_out, nor_3_out, CK);
  and and_2 (and_2_out, CK, nor_4_out);
  nor nor_5 (Q, and_1_out, R, nQ);
  nor nor_6 (nQ, Q, and_2_out);
endmodule

module D1R (
  input  in_1,
  input  in_2,
  input  in_3,
  input  in_4,
  output out_5
);

  wire buffer_1_out, nfet_1_out_3, nfet_2_out_3;

  buf buffer_1 (buffer_1_out, nfet_1_out_3);
  nFet nfet_1 (.in_2(in_3), .out_3(nfet_1_out_3), .in_1(in_1));
  nFet nfet_2 (.in_2(buffer_1_out), .out_3(nfet_2_out_3), .in_1(in_2));
  nor nor_1 (out_5, ~nfet_2_out_3, in_4);  // NOR_Gate
endmodule

module NOTn (
  input  in_1,
  output out_2
);

  Pull_Resistor #(.pull(1)) pull_resistor_1 (.node(in_1));

  assign out_2 = in_1;
endmodule

module Nbuffer (
  input  in_1,
  output out_2
);

  D_Flip_Flop #(.trigger("low")) d_ff_1 (.clk(1'b0), .D(in_1), .Q(out_2));  // open: Qn, preset, en, reset
endmodule

module nFet (
  input  in_1,
  input  in_2,
  output out_3
);

  D_Flip_Flop #(.trigger("high")) d_ff_1 (.clk(in_1), .D(in_2), .Q(out_3));  // open: Qn, preset, en, reset
endmodule

module DL (
  input  H1,
  input  H2,
  input  in,
  input  R,
  output out
);

  wire nfet_1_out_3, nfet_2_out_3, nfet_3_out_3, nor_1_out;

  nFet nfet_1 (.in_2(out), .out_3(nfet_1_out_3), .in_1(H1));
  nFet nfet_2 (.in_2(in), .out_3(nfet_2_out_3), .in_1(H1));
  nor nor_1 (nor_1_out, nfet_1_out_3, nfet_2_out_3);
  nFet nfet_3 (.in_2(nor_1_out), .out_3(nfet_3_out_3), .in_1(H2));
  nor nor_2 (out, nfet_3_out_3, R);
endmodule

module mot_latch_cell (
  input  H2,
  input  H1,
  input  SEC,
  input  plup,
  output out_5,
  output out_6,
  output out_7
);

  wire buffer_1_out, buffer_2_out, M0ec, nfet_1_out_3, nfet_2_out_3, nfet_3_out_3, nfet_4_out_3,
       nfet_5_out_3, nor_1_out, nor_2_out;

  nand nand_1 (M0ec, H1, nor_1_out);
  nFet nfet_1 (.in_2(nor_2_out), .out_3(nfet_1_out_3), .in_1(H2));
  nor nor_1 (nor_1_out, nfet_1_out_3, buffer_1_out);
  buf buffer_1 (buffer_1_out, nfet_2_out_3);
  nFet nfet_2 (.in_2(buffer_2_out), .out_3(nfet_2_out_3), .in_1(H2));
  nor nor_2 (nor_2_out, nfet_3_out_3, nfet_4_out_3);
  buf buffer_2 (buffer_2_out, nfet_5_out_3);
  nFet nfet_3 (.in_2(nor_1_out), .out_3(nfet_3_out_3), .in_1(H1));
  nFet nfet_4 (.in_2(SEC), .out_3(nfet_4_out_3), .in_1(H1));
  nFet nfet_5 (.in_2(plup), .out_3(nfet_5_out_3), .in_1(H1));

  assign out_5 = H2;
  assign out_6 = H1;
  assign out_7 = SEC;
endmodule

module missile (
  input  MOTCK,
  input  RESET,
  input  M1EC,
  input  M0EN,
  input  D0,
  input  D1,
  input  D2,
  input  D4,
  input  D5,
  output M0
);

  wire and_1_out, d1_1_out, d1_2_out, d1_3_out, d1r_1_out_5, d1r_2_out_5, d1r_3_out_5, d1r_4_out_5,
       d1r_5_out_5, d1r_6_out_5, f1_1_nq, f1_1_q, f1_2_nq, f1_2_q, nor_2_out, nor_3_out, nor_4_out,
       nor_5_out, nor_6_out, nor_7_out, nor_8_out, nor_9_out, nor_10_out, nor_11_out, nor_12_out, nor_13_out,
       nor_14_out, nor_15_out, nor_16_out, nor_17_out, nor_18_out, nor_19_out, nor_20_out, not_1_out,
       not_2_out, not_3_out, not_4_out, not_5_out, not_6_out, not_7_out, not_8_out, not_9_out, not_10_out,
       not_11_out, not_c_1_out_3;

  nor nor_1 (M0, nor_3_out, nor_4_out);
  nor nor_2 (nor_2_out, nor_6_out, nor_9_out, not_3_out);
  nor nor_3 (nor_3_out, nor_2_out, M0EN, d1_2_out);
  nor nor_4 (nor_4_out, M0EN, D5, d1_1_out, D4);
  not not_1 (not_1_out, M1EC);
  nor nor_5 (nor_5_out, not_1_out, MOTCK);
  not not_2 (not_2_out, nor_5_out);
  NOT_c not_c_1 (.B(nor_5_out), .A(not_2_out), .out_3(not_c_1_out_3));
  nor nor_6 (nor_6_out, f1_2_nq, D4);
  not not_3 (not_3_out, D5);
  F1 f1_1 (.nS(f1_2_q), .nR(f1_2_nq), .Q(f1_1_q), .nQ(f1_1_nq), .CK(not_c_1_out_3), .R(RESET));
  nor nor_7 (nor_7_out, RESET, nor_8_out);
  D1 d1_1 (.Out(d1_1_out), .In(d1_2_out), .H2(nor_9_out), .H1(nor_10_out));
  F1 f1_2 (.nS(f1_1_nq), .nR(f1_1_q), .Q(f1_2_q), .nQ(f1_2_nq), .CK(not_c_1_out_3), .R(RESET));
  nor nor_8 (nor_8_out, nor_7_out, not_4_out);
  D1 d1_2 (.Out(d1_2_out), .In(nor_12_out), .H2(nor_9_out), .H1(nor_10_out));
  nor nor_9 (nor_9_out, f1_1_nq, f1_2_nq);
  nor nor_10 (nor_10_out, f1_1_q, f1_2_q);
  not not_4 (not_4_out, f1_2_nq);
  not not_5 (not_5_out, d1_3_out);
  D1 d1_3 (.Out(d1_3_out), .In(nor_11_out), .H2(nor_9_out), .H1(nor_10_out));
  nor nor_11 (nor_11_out, nor_8_out, nor_14_out, nor_13_out);
  nor nor_12 (nor_12_out, nor_14_out, nor_15_out, nor_16_out, nor_17_out);
  nor nor_13 (nor_13_out, not_6_out, not_7_out, not_8_out, not_9_out, not_10_out, not_11_out);
  nor nor_14 (nor_14_out, not_6_out, d1r_2_out_5, not_8_out, not_9_out, d1r_5_out_5, not_11_out);
  nor nor_15 (nor_15_out, not_6_out, not_7_out, nor_18_out, not_8_out, d1r_4_out_5, d1r_5_out_5, D0, d1r_6_out_5);
  nor nor_16 (nor_16_out, not_6_out, d1r_2_out_5, nor_18_out, not_8_out, not_9_out, D1, not_10_out, not_11_out);
  nor nor_17 (nor_17_out, not_6_out, not_7_out, nor_18_out, not_8_out, D2, d1r_4_out_5, d1r_5_out_5, not_11_out);
  D1R d1r_1 (.in_3(nor_19_out), .out_5(d1r_1_out_5), .in_1(nor_10_out), .in_2(nor_9_out), .in_4(not_5_out));
  not not_6 (not_6_out, d1r_1_out_5);
  D1R d1r_2 (.in_3(d1r_1_out_5), .out_5(d1r_2_out_5), .in_1(nor_10_out), .in_2(nor_9_out), .in_4(not_5_out));
  D1R d1r_3 (.in_3(d1r_2_out_5), .out_5(d1r_3_out_5), .in_1(nor_10_out), .in_2(nor_9_out), .in_4(not_5_out));
  not not_7 (not_7_out, d1r_2_out_5);
  nor nor_18 (nor_18_out, D0, D2);
  D1R d1r_4 (.in_3(d1r_3_out_5), .out_5(d1r_4_out_5), .in_1(nor_10_out), .in_2(nor_9_out), .in_4(not_5_out));
  not not_8 (not_8_out, d1r_3_out_5);
  D1R d1r_5 (.in_3(d1r_4_out_5), .out_5(d1r_5_out_5), .in_1(nor_10_out), .in_2(nor_9_out), .in_4(not_5_out));
  not not_9 (not_9_out, d1r_4_out_5);
  D1R d1r_6 (.in_3(d1r_5_out_5), .out_5(d1r_6_out_5), .in_1(nor_10_out), .in_2(nor_9_out), .in_4(not_5_out));
  not not_10 (not_10_out, d1r_5_out_5);
  nor nor_19 (nor_19_out, and_1_out, nor_20_out);
  nor nor_20 (nor_20_out, d1r_5_out_5, not_11_out);
  and and_1 (and_1_out, d1r_5_out_5, not_11_out);
  not not_11 (not_11_out, d1r_6_out_5);
endmodule

module D1 (
  input  H2,
  input  H1,
  input  In,
  output Out
);

  wire buffer_2_out, nfet_1_out_3, nfet_2_out_3;

  nFet nfet_1 (.in_2(buffer_2_out), .out_3(nfet_1_out_3), .in_1(H2));
  buf buffer_1 (Out, nfet_1_out_3);
  buf buffer_2 (buffer_2_out, nfet_2_out_3);
  nFet nfet_2 (.in_2(In), .out_3(nfet_2_out_3), .in_1(H1));
endmodule

module audio (
  input  T2,
  input  T1,
  input  D0,
  input  D1,
  input  D2,
  input  D3,
  output out_7,
  output out_8,
  output out_9,
  output out_10,
  output out_11,
  output OUTPUT,
  output out_13,
  output out_14,
  output out_15,
  output out_16
);

  wire and_1_out, and_2_out, and_3_out, and_4_out, and_5_out, and_6_out, and_7_out, and_8_out, and_9_out,
       and_10_out, and_11_out, and_12_out, and_13_out, aud_ctrl_reg_1_out_2, aud_ctrl_reg_2_out_2,
       aud_ctrl_reg_3_out_2, aud_ctrl_reg_3_out_3, aud_ctrl_reg_4_out_2, aud_ctrl_reg_4_out_3,
       invertedsr_1_out_4, invertedsr_2_out_5, invertedsr_3_out_4, invertedsr_4_out_5, nbuffer_1_out_2,
       nfet_1_out_3, nfet_2_out_3, nor_1_out, nor_2_out, nor_3_out, nor_4_out, nor_5_out, nor_6_out,
       nor_7_out, nor_8_out, nor_9_out, nor_10_out, nor_11_out, nor_12_out, not_1_out, not_2_out, not_3_out,
       not_4_out, not_5_out, not_6_out, not_7_out, not_8_out;

  not not_1 (not_1_out, nor_1_out);
  nor nor_1 (nor_1_out, and_3_out, nor_2_out, and_2_out, and_1_out);
  aud_ctrl_reg aud_ctrl_reg_1 (.in_1(D0), .out_2(aud_ctrl_reg_1_out_2));  // open: out_3
  aud_ctrl_reg aud_ctrl_reg_2 (.in_1(D1), .out_2(aud_ctrl_reg_2_out_2));  // open: out_3
  aud_ctrl_reg aud_ctrl_reg_3 (.in_1(D2), .out_2(aud_ctrl_reg_3_out_2), .out_3(aud_ctrl_reg_3_out_3));
  aud_ctrl_reg aud_ctrl_reg_4 (.in_1(D3), .out_2(aud_ctrl_reg_4_out_2), .out_3(aud_ctrl_reg_4_out_3));
  and and_1 (and_1_out, ~out_7, ~out_8, ~out_9, ~out_10, ~out_11, ~nor_6_out);  // AND_Gate
  and and_2 (and_2_out, out_11, nor_4_out);
  nor nor_2 (nor_2_out, out_11, nor_4_out);
  DI_right di_right_1 (.In(not_1_out), .Out(out_7), .H2(T1), .H1(T2));
  DI_right di_right_2 (.In(out_7), .Out(out_8), .H2(T1), .H1(T2));
  nor nor_3 (nor_3_out, not_2_out, nor_5_out);
  nor nor_4 (nor_4_out, nor_3_out, and_4_out);
  and and_3 (and_3_out, ~aud_ctrl_reg_1_out_2, ~aud_ctrl_reg_2_out_2, ~aud_ctrl_reg_3_out_2, ~aud_ctrl_reg_4_out_2);  // AND_Gate
  DI_right di_right_3 (.In(out_8), .Out(out_9), .H2(T1), .H1(T2));
  not not_2 (not_2_out, out_9);
  nor nor_5 (nor_5_out, aud_ctrl_reg_2_out_2, aud_ctrl_reg_1_out_2);
  and and_4 (and_4_out, nor_5_out, out_16);
  and and_5 (and_5_out, ~nor_7_out, ~aud_ctrl_reg_3_out_2, ~aud_ctrl_reg_4_out_2);  // AND_Gate
  DI_right di_right_4 (.In(out_9), .Out(out_10), .H2(T1), .H1(T2));
  not not_3 (not_3_out, out_10);
  and and_6 (and_6_out, ~nor_8_out, ~aud_ctrl_reg_3_out_3, ~aud_ctrl_reg_4_out_3);  // AND_Gate
  DI_right di_right_5 (.In(out_10), .Out(out_11), .H2(T1), .H1(T2));
  and and_7 (and_7_out, ~out_13, ~aud_ctrl_reg_3_out_3, ~aud_ctrl_reg_4_out_2);  // AND_Gate
  nFet nfet_1 (.in_2(out_11), .out_3(nfet_1_out_3), .in_1(T1));
  not not_4 (not_4_out, aud_ctrl_reg_2_out_2);
  nor nor_6 (nor_6_out, aud_ctrl_reg_1_out_2, aud_ctrl_reg_2_out_2, and_12_out);
  and and_8 (and_8_out, ~nbuffer_1_out_2, ~aud_ctrl_reg_3_out_2, ~aud_ctrl_reg_4_out_3);  // AND_Gate
  nor nor_7 (nor_7_out, and_12_out, nor_9_out, and_10_out);
  Nbuffer nbuffer_1 (.in_1(nfet_1_out_3), .out_2(nbuffer_1_out_2));
  not not_5 (not_5_out, aud_ctrl_reg_1_out_2);
  and and_9 (and_9_out, ~out_7, ~out_8, ~out_9, ~not_3_out, ~aud_ctrl_reg_1_out_2, ~not_4_out);  // AND_Gate
  nor nor_8 (nor_8_out, and_13_out, invertedsr_3_out_4);
  nor nor_9 (nor_9_out, invertedsr_3_out_4, out_16);
  and and_10 (and_10_out, invertedsr_3_out_4, out_16);
  nor nor_10 (nor_10_out, nbuffer_1_out_2, not_5_out, not_4_out);
  nor nor_11 (nor_11_out, nor_10_out, not_4_out, and_9_out);
  and and_11 (and_11_out, ~and_3_out, ~and_5_out, ~and_6_out, ~and_7_out, ~and_8_out);  // AND_Gate
  not not_6 (not_6_out, T2);
  nFet nfet_2 (.in_2(nor_11_out), .out_3(nfet_2_out_3), .in_1(T1));
  not not_7 (not_7_out, and_11_out);
  and and_12 (and_12_out, ~out_13, ~out_14, ~out_15, ~out_16);  // AND_Gate
  and and_13 (and_13_out, ~invertedsr_1_out_4, ~out_14, ~invertedsr_3_out_4);  // AND_Gate
  nor nor_12 (nor_12_out, not_6_out, nfet_2_out_3);
  invertedSR invertedsr_1 (
    .in_2(not_7_out), .in_3(and_11_out), .out_4(invertedsr_1_out_4), .out_5(out_13), .in_1(not_8_out));
  not not_8 (not_8_out, nor_12_out);
  invertedSR invertedsr_2 (
    .in_2(invertedsr_1_out_4), .in_3(out_13), .out_4(out_14), .out_5(invertedsr_2_out_5), .in_1(not_8_out));
  invertedSR invertedsr_3 (
    .in_2(out_14), .in_3(invertedsr_2_out_5), .out_4(invertedsr_3_out_4), .out_5(out_15), .in_1(not_8_out));
  invertedSR invertedsr_4 (
    .in_2(invertedsr_3_out_4), .in_3(out_15), .out_4(out_16), .out_5(invertedsr_4_out_5), .in_1(not_8_out));
  not not_9 (OUTPUT, invertedsr_4_out_5);
endmodule

module DI_right (
  input  H2,
  input  H1,
  input  In,
  output Out
);

  wire buffer_1_out, nfet_1_out_3, nfet_2_out_3;

  nFet nfet_1 (.in_2(In), .out_3(nfet_1_out_3), .in_1(H2));
  buf buffer_1 (buffer_1_out, nfet_1_out_3);
  nFet nfet_2 (.in_2(buffer_1_out), .out_3(nfet_2_out_3), .in_1(H1));
  buf buffer_2 (Out, nfet_2_out_3);
endmodule

module aud_ctrl_reg (
  input  in_1,
  output out_2,
  output out_3
);

  not not_1 (out_3, in_1);

  assign out_2 = in_1;
endmodule

module invertedSR (
  input  in_1,
  input  in_2,
  input  in_3,
  output out_4,
  output out_5
);

  wire not_1_out, not_2_out;

  not not_1 (not_1_out, in_2);
  not not_2 (not_2_out, in_3);
  S_R_Flip_Flop s_r_ff_1 (.S(not_1_out), .clk(in_1), .R(not_2_out), .Q(out_4), .Qn(out_5));  // open: preset, reset, en
endmodule

module test (
  input  a,
  input  b,
  output x
);

  wire and_1_out, and_2_out, not_1_out, not_2_out;

  not not_1 (not_1_out, a);
  not not_2 (not_2_out, b);
  and and_1 (and_1_out, not_1_out, not_2_out);
  and and_2 (and_2_out, a, b);
  or or_1 (x, and_1_out, and_2_out);
endmodule

module test2 (
  input  a,
  input  b,
  output x
);

  xnor xnor_1 (x, a, b);
endmodule
